# Fritzing sketch RelogioBCD (saved by Fritzing 0.9.3b)
circuit board: 8.46667cm x 5.64444cm

parts:
  IC1 = Voltage Regulator LM1117 [package=sot223]
  U3 = USB connector [package=THT]
  Disp1 = LBT2088AH [part_number=LBT2088AH]
  R4 = Resistor [tolerance=±5% resistance=150 package=THT]
  R2 = Resistor [tolerance=±5% resistance=150 package=THT]
  R5 = Resistor [tolerance=±5% resistance=150 package=THT]
  R3 = Resistor [tolerance=±5% resistance=150 package=THT]
  R8 = Resistor [tolerance=±5% resistance=10k package=THT]
  U1 = ESP-12F (ESP8266 WiFi Module) [part_number=ESP8266]

nets:
  N1: IC1.ADJ, R8.Pin_1, U1.GND
  N2: IC1.OUT, U1.VCC
  N3: IC1.IN, U3.5V
  N4: Disp1.pin1, R2.Pin_1
  N5: Disp1.pin2, R3.Pin_1
  N6: Disp1.pin_3, U1.GPIO5
  N7: Disp1.pin_4, U1.GPIO4
  N8: Disp1.pin_5, R5.Pin_0
  N9: Disp1.pin_6, U1.GPIO0
  N10: Disp1.pin_7, R4.Pin_0
  N11: Disp1.pin_10, U1.GPIO13
  N12: Disp1.pin_11, U1.GPIO12
  N13: Disp1.pin_15, U1.GPIO14
  N14: Disp1.pin_16, U1.GPIO16
  N15: R4.Pin_1, R8.Pin_0, U1.GPIO15
  N16: R2.Pin_0, U1.TXD0
  N17: R5.Pin_1, U1.GPIO2
  N18: R3.Pin_0, U1.RXD0

custom parts:
  ESP-12F (ESP8266 WiFi Module): WiFi Module based on the ESP8266 with onboard PCB antenna and UART communications
